// Digital circuit clase.dig as structural Verilog
module clase (
  input  [3:0] A,
  input  [3:0] B,
  input  [3:0] C,
  input  [3:0] C_2,
  input  [3:0] in_7,
  input  A_2,
  input  B_2,
  input  in_15,
  output [3:0] carry,
  output [3:0] Q,
  output [3:0] out_8,
  output carry_2,
  output out_12,
  output out_13,
  output out_14
);

  wire [3:0] and_1_out, and_2_out, and_3_out, and_4_out, and_5_out, and_6_out, not_1_out, not_2_out,
       not_3_out, xor_1_out, xor_2_out, xor_3_out, xor_4_out;

  assign xor_1_out = A ^ B;  // XOr xor_1, 4 bits wide
  assign xor_2_out = A ^ B;  // XOr xor_2, 4 bits wide
  assign not_1_out = ~A;  // Not not_1, 4 bits wide
  assign and_1_out = A & B;  // And and_1, 4 bits wide
  assign and_2_out = xor_1_out & C;  // And and_2, 4 bits wide
  assign and_3_out = B & not_1_out;  // And and_3, 4 bits wide
  Add add_1 (.a(A_2), .b(B_2), .c_i(in_15), .s(out_12), .c_o(carry_2));
  assign xor_3_out = xor_1_out ^ C;  // XOr xor_3, 4 bits wide
  assign not_2_out = ~xor_2_out;  // Not not_2, 4 bits wide
  Sub sub_1 (.a(A_2), .b(B_2), .c_i(in_15), .s(out_14), .c_o(out_13));
  assign xor_4_out = in_7 ^ xor_2_out;  // XOr xor_4, 4 bits wide
  assign and_4_out = not_2_out & in_7;  // And and_4, 4 bits wide
  assign carry = and_1_out | and_2_out;  // Or or_1, 4 bits wide
  assign out_8 = and_4_out ^ and_3_out;  // XOr xor_5, 4 bits wide
  assign not_3_out = ~C_2;  // Not not_3, 4 bits wide
  assign and_5_out = xor_3_out & not_3_out;  // And and_5, 4 bits wide
  assign and_6_out = xor_4_out & C_2;  // And and_6, 4 bits wide
  assign Q = and_5_out | and_6_out;  // Or or_2, 4 bits wide

  // Notes on the sheet:
  //   sumador 4bits
  //   restador 4 bits
  //   mux 2 a 1 de 4 bits
endmodule
